// Logisim project L8.circ as structural Verilog: 5 circuits, main circuit main
module main (
);

  wire clock_1_out, ctrl_1_cf, ctrl_1_cn, ctrl_1_ip, ctrl_1_jmp, ctrl_1_m, ctrl_1_muxa, ctrl_1_muxb,
       ctrl_1_step, n7476_1_nq, n74688_1_p_q, not_1_out, not_2_out, not_3_out, not_4_out;
  wire [2:0] ctrl_1_state;
  wire [3:0] ctrl_1_fn_sel, IR_q, IR_q_2;
  wire [6:0] ctrl_1_mar;
  wire [7:0] ALU_f, IP_q, MAR_q, MBR_q, multiplexer_1_out, multiplexer_2_out, ram_1_data, reg_1_qa, reg_1_qb,
       register_1_q;
  wire [31:0] reg_1_test;

  Clock clock_1 (.out(clock_1_out));
  IP IP (.in_1(MBR_q), .EN(ctrl_1_ip), .LD(ctrl_1_jmp), .CLK(clock_1_out), .Q(IP_q));
  // Probe on IP_q
  Multiplexer #(.width(8), .enable("false")) multiplexer_1 (
    .in0(MBR_q), .in1(IP_q), .out(multiplexer_1_out), .sel(ctrl_1_muxa));
  // Probe on ctrl_1_state
  ctrl ctrl_1 (
    .clock(clock_1_out), .IR(IR_q), .y(IR_q_2[1:0]), .zero(n7476_1_nq), .state(ctrl_1_state),
    .MAR(ctrl_1_mar[0]), .IP(ctrl_1_ip), .IR_2(ctrl_1_mar[2]), .MBR(ctrl_1_mar[3]), .WR(ctrl_1_mar[4]),
    .WM(ctrl_1_mar[5]), .MUXa(ctrl_1_muxa), .MUXb(ctrl_1_muxb), .step(ctrl_1_step), .FN_SEL(ctrl_1_fn_sel),
    .m(ctrl_1_m), .cn(ctrl_1_cn), .jmp(ctrl_1_jmp), .z(ctrl_1_mar[6]), .cf(ctrl_1_cf));
  Register MAR (.D(multiplexer_1_out), .Q(MAR_q), .clk(register_1_q[0]));  // open: en, clr
  not not_1 (not_1_out, register_1_q[5]);
  not not_2 (not_2_out, register_1_q[5]);
  Register register_1 (
    .D({1'b0, ctrl_1_mar[6:2], 1'b0, ctrl_1_mar[0]}), .Q(register_1_q), .clk(clock_1_out));  // open: en, clr
  // Probe on ram_1_data
  RAM #(.bus("asynch")) ram_1 (.addr(MAR_q), .data(ram_1_data), .ld(not_1_out));  // open: sel, clr
  Register IR (.D(ram_1_data), .Q({IR_q, IR_q_2}), .clk(register_1_q[2]));  // open: en, clr
  // Probe on IR_q_2[3:2]
  // Probe on IR_q_2[1:0]
  Register MBR (.D(ALU_f), .Q(MBR_q), .clk(register_1_q[3]));  // open: en, clr
  not not_3 (not_3_out, not_2_out);
  \reg  reg_1 (
    .GrA(1'b0), .RA(IR_q_2[3:2]), .D(MBR_q), .Gw(register_1_q[4]), .wa(IR_q_2[3:2]), .GrB(1'b0),
    .RB(IR_q_2[1:0]), .Qa(reg_1_qa), .Qb(reg_1_qb), .test(reg_1_test));
  // Probe on reg_1_test
  assign ram_1_data = not_3_out ? MBR_q : 8'bz;  // Controlled_Buffer controlled_buffer_1
  Multiplexer #(.width(8), .enable("false")) multiplexer_2 (
    .in0(ram_1_data), .in1(reg_1_qa), .out(multiplexer_2_out), .sel(ctrl_1_muxb));
  // Probe on ram_1_data
  // Probe on multiplexer_2_out
  // Probe on reg_1_qb
  alu ALU (
    .A(multiplexer_2_out), .B(reg_1_qb), .M(ctrl_1_m), .Cn(ctrl_1_cn), .S(ctrl_1_fn_sel), .F(ALU_f));  // open: Cn_4, A_B
  // Probe on ALU_f
  _74688 u_74688_1 (.P(MBR_q), .Q({8{1'b0}}), .nE(1'b0), .P_Q(n74688_1_p_q));
  not not_4 (not_4_out, n74688_1_p_q);
  _7476 u_7476_1 (
    .J(not_4_out), .CK(register_1_q[6]), .K(1'b0), .nRD(ctrl_1_cf), .nSD(1'b1), .nQ(n7476_1_nq));  // open: Q
endmodule

module ctrl (
  input  clock,
  input  [3:0] IR,
  input  [1:0] y,
  input  zero,
  output [2:0] state,
  output MAR,
  output IP,
  output IR_2,
  output MBR,
  output WR,
  output WM,
  output MUXa,
  output MUXb,
  output step,
  output [3:0] FN_SEL,
  output m,
  output cn,
  output jmp,
  output z,
  output cf
);

  wire ADC, ADD, AND, and_1_out, HLT, IN_OUT, INC, JMP_t, LD, multiplexer_1_out, multiplexer_7_out, NOT,
       not_1_out, not_2_out, not_3_out, not_5_out, not_6_out, OR, or_1_out, or_2_out, SBC, STR, SUB, T0, T1,
       T2, T3, T5, tunnel, XOR, ZF;

  _74154 u_74154_1 (
    .E0(1'b0), .E1(1'b0), .A0(IR[0]), .A1(IR[1]), .A2(IR[2]), .A3(IR[3]), .Y0(HLT), .Y1(ADD), .Y2(ADC),
    .Y3(SUB), .Y4(SBC), .Y5(AND), .Y6(OR), .Y7(XOR), .Y8(NOT), .Y9(INC), .Y10(ZF), .Y11(JMP_t), .Y12(tunnel),
    .Y13(IN_OUT), .Y14(LD), .Y15(STR));
  not not_1 (not_1_out, clock);
  Multiplexer #(.select(3), .disabled(0)) multiplexer_1 (
    .in0(1'b1), .in1(1'b1), .in2(1'b1), .in3(T1), .in4(1'b1), .in5(T2), .in6(1'b1), .in7(T1),
    .out(multiplexer_1_out), .sel({y[0], LD, STR}), .en(or_1_out));
  _74163 u_74163_1 (
    .D0(1'b1), .D1(1'b0), .D2(1'b1), .D3(1'b0), .CET(1'b1), .CEP(1'b1), .nPE(multiplexer_1_out), .nMR(step),
    .CP(not_1_out), .Q0(state[0]), .Q1(state[1]), .Q2(state[2]));  // open: Q3, TC
  or or_1 (or_1_out, T5, HLT);
  _74138 u_74138_1 (
    .E3(1'b1), .E2(1'b0), .E1(1'b0), .A0(state[0]), .A1(state[1]), .A2(state[2]), .Y0(T0), .Y1(T1), .Y2(T2),
    .Y3(T3), .Y4(MUXa), .Y5(T5), .Y6(step));  // open: Y7
  or or_2 (or_2_out, T5, LD, not_2_out);
  not not_2 (not_2_out, y[0]);
  Multiplexer #(.select(3), .disabled(0)) multiplexer_2 (
    .in0(1'b0), .in1(1'b1), .in2(1'b1), .in3(1'b0), .in4(1'b0), .in5(1'b1), .in6(1'b0), .in7(1'b0),
    .out(FN_SEL[3]), .sel(IR[2:0]), .en(not_3_out));
  Multiplexer #(.select(3), .disabled(0)) multiplexer_3 (
    .in0(1'b0), .in1(1'b0), .in2(1'b0), .in3(1'b1), .in4(1'b1), .in5(1'b1), .in6(1'b1), .in7(1'b1),
    .out(FN_SEL[2]), .sel(IR[2:0]), .en(not_3_out));
  Multiplexer #(.select(3), .disabled(0)) multiplexer_4 (
    .in0(1'b0), .in1(1'b0), .in2(1'b0), .in3(1'b1), .in4(1'b1), .in5(1'b0), .in6(1'b1), .in7(1'b1),
    .out(FN_SEL[1]), .sel(IR[2:0]), .en(not_3_out));
  Multiplexer #(.select(3), .disabled(0)) multiplexer_5 (
    .in0(1'b0), .in1(1'b1), .in2(1'b1), .in3(1'b0), .in4(1'b0), .in5(1'b1), .in6(1'b1), .in7(1'b0),
    .out(FN_SEL[0]), .sel(IR[2:0]), .en(not_3_out));
  not not_3 (not_3_out, IR[3]);
  nand nand_1 (MAR, T0, T2, MUXa);
  nand nand_2 (IP, T1, T3, or_2_out);
  not not_4 (IR_2, T1);
  nand nand_3 (MBR, T3, T5);
  nand nand_4 (WR, STR, ~step);  // NAND_Gate
  nor nor_1 (WM, STR, step);
  nor nor_2 (MUXb, T5, ~LD);  // NOR_Gate
  not not_5 (not_5_out, JMP_t);
  and and_1 (and_1_out, XOR, SUB, INC, ADD);
  nand nand_5 (m, AND, OR, XOR, NOT);
  Multiplexer #(.select(3), .enable("false")) multiplexer_6 (
    .in0(1'b1), .in1(1'b1), .in2(1'b1), .in3(T5), .in4(1'b1), .in5(T5), .in6(T5), .in7(1'b1), .out(cn),
    .sel({INC, SUB, ADC}));
  Multiplexer #(.select(3), .disabled(0)) multiplexer_7 (
    .in0(not_5_out), .in1(1'b0), .in2(1'b0), .in3(1'b0), .in4(not_5_out), .in5(not_5_out), .in6(1'b0),
    .in7(1'b0), .out(multiplexer_7_out), .sel({zero, y}), .en(not_6_out));
  not not_6 (not_6_out, step);
  nor nor_3 (z, and_1_out, step);
  or or_3 (cf, ZF, step);
  not not_7 (jmp, multiplexer_7_out);

  // Other names for the same wires on the sheet: T4 = MUXa; T6 = step
endmodule

module IP (
  input  [7:0] in_1,
  input  EN,
  input  LD,
  input  CLK,
  output [7:0] Q
);

  wire n74163_1_tc;

  _74163 u_74163_1 (
    .D0(in_1[0]), .D1(in_1[1]), .D2(in_1[2]), .D3(in_1[3]), .CET(EN), .CEP(EN), .nPE(LD), .nMR(1'b1),
    .CP(CLK), .Q0(Q[0]), .Q1(Q[1]), .Q2(Q[2]), .Q3(Q[3]), .TC(n74163_1_tc));
  _74163 u_74163_2 (
    .D0(in_1[4]), .D1(in_1[5]), .D2(in_1[6]), .D3(in_1[7]), .CET(n74163_1_tc), .CEP(EN), .nPE(LD),
    .nMR(1'b1), .CP(CLK), .Q0(Q[4]), .Q1(Q[5]), .Q2(Q[6]), .Q3(Q[7]));  // open: TC
endmodule

module alu (
  input  [7:0] A,
  input  [7:0] B,
  input  M,
  input  Cn,
  input  [3:0] S,
  output Cn_4,
  output A_B,
  output [7:0] F
);

  wire n74181_1_a_b, n74181_1_cn_4, n74181_2_a_b;

  _74181 u_74181_1 (
    .S3(S[3]), .S2(S[2]), .S1(S[1]), .S0(S[0]), .B3(B[3]), .A3(A[3]), .B2(B[2]), .A2(A[2]), .B1(B[1]),
    .A1(A[1]), .B0(B[0]), .A0(A[0]), .M(M), .Cn(Cn), .Cn_4(n74181_1_cn_4), .F3(F[3]), .F2(F[2]),
    .A_B(n74181_1_a_b), .F1(F[1]), .F0(F[0]));  // open: G, P
  _74181 u_74181_2 (
    .S3(S[3]), .S2(S[2]), .S1(S[1]), .S0(S[0]), .B3(B[7]), .A3(A[7]), .B2(B[6]), .A2(A[6]), .B1(B[5]),
    .A1(A[5]), .B0(B[4]), .A0(A[4]), .M(M), .Cn(n74181_1_cn_4), .Cn_4(Cn_4), .F3(F[7]), .F2(F[6]),
    .A_B(n74181_2_a_b), .F1(F[5]), .F0(F[4]));  // open: G, P
  and and_1 (A_B, n74181_1_a_b, n74181_2_a_b);
endmodule

module \reg  (
  input  GrA,
  input  [1:0] RA,
  input  [7:0] D,
  input  Gw,
  input  [1:0] wa,
  input  GrB,
  input  [1:0] RB,
  output [7:0] Qa,
  output [7:0] Qb,
  output [31:0] test
);

  wire decoder_1_out0, decoder_1_out1, decoder_1_out2, decoder_1_out3, decoder_2_out0, decoder_2_out1,
       decoder_2_out2, decoder_2_out3, not_1_out, not_2_out, not_3_out, not_4_out;
  wire [7:0] register_1_q, register_3_q, register_5_q, register_7_q;

  not not_1 (not_1_out, Gw);
  Decoder #(.select(2), .disabled(0), .enable("false")) decoder_1 (
    .out0(decoder_1_out0), .out1(decoder_1_out1), .out2(decoder_1_out2), .out3(decoder_1_out3), .sel(wa));
  not not_2 (not_2_out, Gw);
  Decoder #(.select(2), .disabled(0), .enable("false")) decoder_2 (
    .out0(decoder_2_out0), .out1(decoder_2_out1), .out2(decoder_2_out2), .out3(decoder_2_out3), .sel(wa));
  Register #(.trigger("high")) register_1 (.D(D), .en(not_1_out), .Q(register_1_q), .clk(decoder_1_out0));  // open: clr
  Register #(.trigger("high")) register_2 (.D(D), .en(not_2_out), .Q(test[7:0]), .clk(decoder_2_out0));  // open: clr
  Register #(.trigger("high")) register_3 (.D(D), .en(not_1_out), .Q(register_3_q), .clk(decoder_1_out1));  // open: clr
  Register #(.trigger("high")) register_4 (.D(D), .en(not_2_out), .Q(test[15:8]), .clk(decoder_2_out1));  // open: clr
  Register #(.trigger("high")) register_5 (.D(D), .en(not_1_out), .Q(register_5_q), .clk(decoder_1_out2));  // open: clr
  Register #(.trigger("high")) register_6 (.D(D), .en(not_2_out), .Q(test[23:16]), .clk(decoder_2_out2));  // open: clr
  not not_3 (not_3_out, GrA);
  Multiplexer #(.select(2), .width(8)) multiplexer_1 (
    .in0(register_1_q), .in1(register_3_q), .in2(register_5_q), .in3(register_7_q), .out(Qa), .sel(RA),
    .en(not_3_out));
  Register #(.trigger("high")) register_7 (.D(D), .en(not_1_out), .Q(register_7_q), .clk(decoder_1_out3));  // open: clr
  not not_4 (not_4_out, GrB);
  Multiplexer #(.select(2), .width(8)) multiplexer_2 (
    .in0(test[7:0]), .in1(test[15:8]), .in2(test[23:16]), .in3(test[31:24]), .out(Qb), .sel(RB),
    .en(not_4_out));
  Register #(.trigger("high")) register_8 (.D(D), .en(not_2_out), .Q(test[31:24]), .clk(decoder_2_out3));  // open: clr
endmodule
